// Logisim project lab3_3.circ as structural Verilog: 1 circuit, main circuit main
module main (
  input  A,
  input  S,
  input  B,
  output out_4
);

  wire not_1_out, S___B_out, S_prime___A_out;

  not not_1 (not_1_out, S);
  and S_prime___A (S_prime___A_out, A, not_1_out);
  and S___B (S___B_out, S, B);
  or S_prime___A_____S___B (out_4, S_prime___A_out, S___B_out);
endmodule
